// Logisim project qualquerSequencia.circ as structural Verilog: 1 circuit, main circuit main
module main (
);

  wire clock_1_out, q3_qn;
  wire [3:0] q0_q;

  Clock clock_1 (.out(clock_1_out));
  J_K_Flip_Flop q3 (.J(q0_q[0]), .clk(clock_1_out), .K(q0_q[1]), .Q(q0_q[3]), .Qn(q3_qn));  // open: preset, en, reset
  J_K_Flip_Flop q2 (.J(q3_qn), .clk(clock_1_out), .K(q0_q[3]), .Q(q0_q[2]));  // open: Qn, preset, en, reset
  J_K_Flip_Flop q1 (.J(1'b1), .clk(clock_1_out), .K(q0_q[2]), .Q(q0_q[1]));  // open: Qn, preset, en, reset
  J_K_Flip_Flop q0 (.J(q3_qn), .clk(clock_1_out), .K(q0_q[3]), .Q(q0_q[0]));  // open: Qn, preset, en, reset
  Hex_Digit_Display hex_digit_display_1 (.value(q0_q));  // open: dp
endmodule
